# Fritzing sketch Støjgenerator med Teensy 41 til produktion (saved by Fritzing 1.0.4)
circuit board: 10.6572cm x 14.7484cm
breadboards: 1

parts:
  4_7kΩ = Resistor [tolerance=±5% power=0.25W resistance=4.7k package=THT]
  10kΩ = Resistor [tolerance=±5% power=0.25W resistance=10k package=THT]
  100kΩ = Resistor [tolerance=±5% power=0.25W resistance=100k package=THT]
  4_7kΩ_2 = Resistor [tolerance=±5% power=0.25W resistance=4.7k package=THT]
  1_5nF = Ceramic Capacitor [capacitance=1.5nF voltage=35V package="100 mil [THT, multilayer]"]
  100kΩ_2 = Resistor [tolerance=±5% power=0.25W resistance=100k package=THT]
  10kΩ_2 = Resistor [tolerance=±5% power=0.25W resistance=10k package=THT]
  100kΩ_3 = Resistor [tolerance=±5% power=0.25W resistance=100k package=THT]
  10kΩ_3 = Resistor [tolerance=±5% power=0.25W resistance=10k package=THT]
  1_5nF_2 = Ceramic Capacitor [capacitance=1.5nF voltage=35V package="100 mil [THT, multilayer]"]
  100kΩ_4 = Resistor [tolerance=±5% power=0.25W resistance=100k package=THT]
  10kΩ_4 = Resistor [tolerance=±5% power=0.25W resistance=10k package=THT]
  1_5nF_3 = Ceramic Capacitor [capacitance=1.5nF voltage=35V package="100 mil [THT, multilayer]"]
  MCP_6024 = MCP6024 [package="DIP (Dual Inline) [THT]"]
  2_4V = DIODE-ZENER [package=diode-zener]
  2_2µF = Ceramic Capacitor [capacitance=2.2µF voltage=35V package="200 mil [THT, multilayer]"]
  2_2µF_2 = Ceramic Capacitor [capacitance=2.2µF voltage=35V package="200 mil [THT, multilayer]"]
  2_2µF_3 = Ceramic Capacitor [capacitance=2.2µF voltage=35V package="200 mil [THT, multilayer]"]
  2_2µF_4 = Ceramic Capacitor [capacitance=2.2µF voltage=35V package="200 mil [THT, multilayer]"]
  1_5nF_4 = Ceramic Capacitor [capacitance=1.5nF voltage=35V package="100 mil [THT, multilayer]"]
  2_7kΩ = Resistor [tolerance=±5% power=0.25W resistance=2700 package=THT]
  Teensy_4_1 = Teensy 4.1

nets:
  N1: 4_7kΩ.Pin_0, MCP_6024.V+, 2_7kΩ.Pin_0, Teensy_4_1.Pin_26, Teensy_4_1.Pin_62
  N2: 4_7kΩ.Pin_1, 4_7kΩ_2.Pin_0, MCP_6024.IN_A+, MCP_6024.IN_B+, MCP_6024.IN_C+, MCP_6024.IN_D+
  N3: 10kΩ.Pin_0, 2_2µF.0
  N4: 10kΩ.Pin_1, 100kΩ.Pin_1, MCP_6024.IN_B-, 1_5nF_4.1
  N5: 100kΩ.Pin_0, MCP_6024.OUT_B, 2_2µF_2.1, 1_5nF_4.0
  N6: 4_7kΩ_2.Pin_1, MCP_6024.V-, 2_4V.A, Teensy_4_1.Pin_11, Teensy_4_1.Pin_12, Teensy_4_1.Pin_50, Teensy_4_1.Pin_63
  N7: 1_5nF.0, 100kΩ_2.Pin_0, MCP_6024.OUT_C, 2_2µF_3.0
  N8: 1_5nF.1, 100kΩ_2.Pin_1, 10kΩ_2.Pin_1, MCP_6024.IN_C-
  N9: 10kΩ_2.Pin_0, 2_2µF_2.0
  N10: 100kΩ_3.Pin_0, 10kΩ_3.Pin_1, 1_5nF_2.0, MCP_6024.IN_D-
  N11: 100kΩ_3.Pin_1, 1_5nF_2.1, MCP_6024.OUT_D, 2_2µF_4.0
  N12: 10kΩ_3.Pin_0, 2_2µF_3.1
  N13: 100kΩ_4.Pin_0, 10kΩ_4.Pin_1, 1_5nF_3.0, MCP_6024.IN_A-
  N14: 100kΩ_4.Pin_1, 1_5nF_3.1, MCP_6024.OUT_A, Teensy_4_1.Pin_52
  N15: 10kΩ_4.Pin_0, 2_2µF_4.1
  N16: 2_4V.C, 2_2µF.1, 2_7kΩ.Pin_1

notes:
  ───────────────────────────────────────────────
  Quantum Entanglement Interface
  Circuit for Mind–Matter Correlation · Jens Klausen 2025

custom parts:
  MCP6024: Microchip MCP6024 quad op-amp, DIP-14
  Teensy 4.1: The Teensy is a complete USB-based microcontoller development system, in a very small footprint, capable of implementing many types of projects. All programming is done via the USB port. No special programmer is needed, only a standard micro-USB cable and a PC or Macintosh with a USB port.
